# Fritzing sketch Diod (saved by Fritzing 0.9.3b)
breadboards: 1

parts:
  Часть1 = Arduino Uno (Rev3)
  R1 = Resistor [tolerance=±5% resistance=220 package=THT]
  LED1 = smd LED [color="Red (633nm)" package="0805 [SMD]"]

nets:
  N1: Часть1.5V, R1.Pin_1
  N2: Часть1.GND, LED1.cathode
  N3: R1.Pin_0, LED1.anode
