# Fritzing sketch Diod222 (saved by Fritzing 0.9.3b)
breadboards: 1

parts:
  Часть1 = Arduino Uno (Rev3)
  R2 = Resistor [tolerance=±5% resistance=220 package=THT]
  LED2 = LED - 5mm [color="Yellow (595nm)" package="5 mm [THT]"]
  LED3 = LED - 5mm [color="Yellow (595nm)" package="5 mm [THT]"]

nets:
  N1: Часть1.5V, LED3.anode
  N2: Часть1.GND, R2.Pin_0
  N3: R2.Pin_1, LED2.cathode
  N4: LED2.anode, LED3.cathode
