# Fritzing sketch DiodButton (saved by Fritzing 0.9.3b)
breadboards: 1

parts:
  Часть1 = Arduino Uno (Rev3)
  R1 = Resistor [tolerance=±5% resistance=220 package=THT]
  LED1 = smd LED [color="Red (633nm)" package="0805 [SMD]"]
  S1 = Pushbutton [package="[THT]"]

nets:
  N1: Часть1.5V, S1.Pin_1, S1.Pin_2
  N2: Часть1.GND, LED1.cathode
  N3: R1.Pin_0, LED1.anode
  N4: R1.Pin_1, S1.Pin_3, S1.Pin_4
