# Fritzing sketch svetlofor (saved by Fritzing 0.9.3b)
breadboards: 1

parts:
  Часть1 = Arduino Uno (Rev3)
  R1 = Resistor [tolerance=±5% resistance=220 package=THT]
  LED1 = LED - 5mm [color="Red (633nm)" package="5 mm [THT]"]
  R2 = Resistor [tolerance=±5% resistance=220 package=THT]
  LED2 = LED - 5mm [color="Yellow (595nm)" package="5 mm [THT]"]
  R3 = Resistor [tolerance=±5% resistance=220 package=THT]
  LED3 = LED - 5mm [color="Green (570nm)" package="5 mm [THT]"]

nets:
  N1: Часть1.GND, R1.Pin_0, R2.Pin_0, R3.Pin_0
  N2: Часть1.D5_PWM, LED3.anode
  N3: Часть1.D6_PWM, LED2.anode
  N4: Часть1.D7, LED1.anode
  N5: R1.Pin_1, LED1.cathode
  N6: R2.Pin_1, LED2.cathode
  N7: R3.Pin_1, LED3.cathode
