# Fritzing sketch pullup (saved by Fritzing 0.9.3b)
breadboards: 1

parts:
  S1 = Pushbutton [package=THT]
  R1 = Resistor [tolerance=±5% resistance=1k package=THT]
  Часть1 = Arduino Uno (Rev3)

nets:
  N1: S1.leg0, R1.Pin_0, Часть1.D2
  N2: S1.leg1, Часть1.GND
  N3: R1.Pin_1, Часть1.5V
