# Fritzing sketch shake (saved by Fritzing 0.9.3b)
breadboards: 1

parts:
  Часть1 = Arduino Uno (Rev3)
  J1 = Piezo Speaker
  LED1 = LED - 5mm [color="Red (633nm)" package="5 mm [THT]"]
  R1 = Resistor [tolerance=±5% resistance=220 package=THT]
  C1 = Electrolytic Capacitor [capacitance=1µF package="100 mil [THT, electrolytic]"]
  R2 = Resistor [tolerance=±5% resistance=220 package=THT]

nets:
  N1: Часть1.GND, J1.pin1, R1.Pin_0, R2.Pin_1
  N2: Часть1.D5_PWM, LED1.anode
  N3: Часть1.D6_PWM, J1.pin2
  N4: Часть1.D7, C1.+, R2.Pin_0
  N5: Часть1.5V, C1.-
  N6: LED1.cathode, R1.Pin_1
