# Fritzing sketch signal_part (saved by Fritzing 0.9.3b)
breadboards: 1

parts:
  J1 = Piezo Speaker  # not connected
  LED1 = LED - 5mm [color="Red (633nm)" package="5 mm [THT]"]
  R1 = Resistor [tolerance=±5% resistance=220 package=THT]

nets:
  N1: LED1.cathode, R1.Pin_1
