# Fritzing sketch LM35 (saved by Fritzing 0.9.3b)
breadboards: 1

parts:
  T1 = LM35 Temperature Sensor [package="TO92 [THT]"]
  Часть1 = Arduino Uno (Rev3)

nets:
  N1: T1.+Vs, Часть1.5V
  N2: T1.Vout, Часть1.A1
  GND: T1.GND, Часть1.GND
