# Fritzing sketch diod (saved by Fritzing 0.9.3b)
breadboards: 1

parts:
  Часть1 = Arduino Uno (Rev3)
  LED1 = LED - 5mm [color="Red (633nm)" package="5 mm [THT]"]
  R1 = Resistor [tolerance=±5% resistance=220 package=THT]

nets:
  N1: Часть1.D11_PWM/MOSI, R1.Pin_1
  N2: Часть1.GND, LED1.cathode
  N3: LED1.anode, R1.Pin_0
