# Fritzing sketch diodRGB (saved by Fritzing 0.9.3b)
breadboards: 1

parts:
  Часть1 = Arduino Uno (Rev3)
  R1 = Resistor [tolerance=±5% resistance=220 package=THT]
  LED2 = RGB LED (com. cathode, rgb) [package="5 mm [THT]"]
  R2 = Resistor [tolerance=±5% resistance=220 package=THT]
  R3 = Resistor [tolerance=±5% resistance=220 package=THT]

nets:
  N1: Часть1.D9_PWM, R3.Pin_1
  N2: Часть1.D10_PWM/SS, R1.Pin_1
  N3: Часть1.D11_PWM/MOSI, R2.Pin_1
  N4: Часть1.GND, LED2.common_cathode
  N5: R1.Pin_0, LED2.green_anode
  N6: LED2.red_anode, R2.Pin_0
  N7: LED2.blue_anode, R3.Pin_0
