# Fritzing sketch diodRGBplusLM35 (saved by Fritzing 0.9.3b)
breadboards: 1

parts:
  Часть1 = Arduino Uno (Rev3)
  R1 = Resistor [tolerance=±5% resistance=220 package=THT]
  LED2 = RGB LED (com. cathode, rgb) [package="5 mm [THT]"]
  R2 = Resistor [tolerance=±5% resistance=220 package=THT]
  R3 = Resistor [tolerance=±5% resistance=220 package=THT]
  T1 = LM35 Temperature Sensor [package="TO92 [THT]"]

nets:
  N1: Часть1.A1, T1.Vout
  N2: Часть1.D9_PWM, R3.Pin_1
  N3: Часть1.D10_PWM/SS, R1.Pin_1
  N4: Часть1.D11_PWM/MOSI, R2.Pin_1
  N5: Часть1.5V, T1.+Vs
  GND: Часть1.GND, LED2.common_cathode, T1.GND
  N6: R1.Pin_0, LED2.green_anode
  N7: LED2.red_anode, R2.Pin_0
  N8: LED2.blue_anode, R3.Pin_0
