# Fritzing sketch nightLampButton (saved by Fritzing 0.9.3b)
breadboards: 1

parts:
  R1 = Resistor [tolerance=±5% resistance=1k package=THT]
  Часть1 = Arduino Uno (Rev3)
  LED1 = LED - 5mm [color="Red (633nm)" package="5 mm [THT]"]
  R3 = Resistor [tolerance=±5% resistance=220 package=THT]
  S1 = Pushbutton [package="[THT]"]
  R4 = Resistor [tolerance=±5% resistance=220 package=THT]
  R5 = Photocell (LDR) [package=THT]

nets:
  N1: R1.Pin_0, Часть1.GND, LED1.cathode, R4.Pin_1
  N2: R1.Pin_1, Часть1.A0, R5.pin_0
  N3: Часть1.D8, R3.Pin_1
  N4: Часть1.D2, S1.Pin_1, S1.Pin_2, R4.Pin_0
  N5: Часть1.5V, S1.Pin_3, S1.Pin_4, R5.pin_1
  N6: LED1.anode, R3.Pin_0
