# Fritzing sketch fotorez (saved by Fritzing 0.9.3b)
breadboards: 1

parts:
  R1 = Resistor [tolerance=±5% resistance=1k package=THT]
  R2 = Photocell (LDR) [package=THT]
  Часть1 = Arduino Uno (Rev3)

nets:
  N1: R1.Pin_0, Часть1.GND
  N2: R1.Pin_1, R2.pin_0, Часть1.A0
  N3: R2.pin_1, Часть1.5V
