# Fritzing sketch nightLamp (saved by Fritzing 0.9.3b)
breadboards: 1

parts:
  R1 = Resistor [tolerance=±5% resistance=1k package=THT]
  R2 = Photocell (LDR) [package=THT]
  Часть1 = Arduino Uno (Rev3)
  LED1 = LED - 5mm [color="Red (633nm)" package="5 mm [THT]"]
  R3 = Resistor [tolerance=±5% resistance=220 package=THT]

nets:
  N1: R1.Pin_0, Часть1.GND, LED1.cathode
  N2: R1.Pin_1, R2.pin_0, Часть1.A0
  N3: R2.pin_1, Часть1.5V
  N4: Часть1.D8, R3.Pin_1
  N5: LED1.anode, R3.Pin_0
